# Fritzing sketch caros-huener (saved by Fritzing 0.9.6b)
breadboards: 1

parts:
  Bauteil1 = Arduino Pro Mini (5V)
  M1 = DC Motor
  R1 = Rotary Potentiometer (Large) [maximum_resistance=100kΩ package=THT]
  S1 = Square Pushbutton
  S2_open = Reed switch [package=THT]
  S3_close = Reed switch [package=THT]
  U1 = L298_BRIDGE_DRIVER [package=powerso20]
  V1_stepdown_7_4_-5V = AC Power [voltage=5 frequency=60]
  R2 = Photocell (LDR) [package=THT]
  R3 = Resistor [tolerance=±5% resistance=220 package=THT]
  S2 = Square Pushbutton
  piepser = Piezo Speaker
  R4 = Resistor [tolerance=±5% resistance=47k package=THT]
  R5 = Resistor [tolerance=±5% resistance=39k package=THT]
  Bauteil2 = Breadboard Power Supply Board SMD

nets:
  VCC: Bauteil1.VCC, U1.VS, V1_stepdown_7_4_-5V.V+, Bauteil2.VCC
  GND: Bauteil1.GND, R1.leg1, S1.leg1, S2_open.pin_1, S3_close.pin_1, U1.GND, V1_stepdown_7_4_-5V.V-, R3.Pin_0, piepser.pin2, Bauteil2.GND
  N1: Bauteil1.A6, R1.wiper
  N2: Bauteil1.A3, R4.Pin_1, R5.Pin_0
  N3: Bauteil1.A1, R2.pin_0, R3.Pin_1
  N4: Bauteil1.D10, piepser.pin1
  N5: Bauteil1.D9, R1.leg2, R2.pin_1
  N6: Bauteil1.D8, S2_open.pin_2
  N7: Bauteil1.D7, S3_close.pin_2
  N8: Bauteil1.D6, U1.IN2
  N9: Bauteil1.D5, U1.IN1
  N10: Bauteil1.D3, S2.leg0
  N11: Bauteil1.D2, S1.leg0
  N12: M1.pin_1, U1.OUT1
  N13: M1.pin_2, U1.OUT2
  N14: R5.Pin_1, Bauteil2.VIN

notes:
  wechselschalter mit 3 pos
